// Logisim project f1fec1d11eadf045.circ as structural Verilog: 3 circuits, main circuit main
module main (
);

  wire _3, and_1_out, and_2_out, and_3_out, and_4_out, and_5_out, and_6_out, and_7_out, and_8_out, and_9_out,
       and_10_out, and_11_out, and_12_out, clock_1_out, controlled_buffer_1_out, d_ff_1_q, d_ff_1_qn,
       d_ff_2_q, d_ff_3_q, d_ff_4_q, or_1_out, RESET_out, \Шарик_на_линии_ракетки_out ;
  wire [2:0] _2, counter_1_q, joystick_1_y;
  wire [7:0] _1, decoder_1_out0, demultiplexer_1_out1, demultiplexer_1_out2, demultiplexer_1_out3,
       demultiplexer_1_out4, demultiplexer_1_out5, demultiplexer_1_out6, demultiplexer_1_out7;

  Button RESET (.out(RESET_out));
  Joystick #(.bits(3)) joystick_1 (.y(joystick_1_y));  // open: x
  and and_1 (and_1_out, ~_2[0], ~_2[1], ~_2[2]);  // AND_Gate
  and and_2 (and_2_out, _2[0], _2[1], _2[2]);
  D_Flip_Flop d_ff_1 (.Q(d_ff_1_q), .Qn(d_ff_1_qn), .preset(and_2_out), .reset(and_1_out));  // open: clk, D, en
  and and_3 (and_3_out, ~counter_1_q[0], ~counter_1_q[1], ~counter_1_q[2]);  // AND_Gate
  Clock clock_1 (.out(clock_1_out));
  and and_4 (and_4_out, counter_1_q[0], counter_1_q[1], counter_1_q[2]);
  D_Flip_Flop d_ff_2 (.Q(d_ff_2_q), .preset(and_4_out), .reset(and_3_out));  // open: clk, D, Qn, en
  D_Flip_Flop #(.trigger("high")) d_ff_3 (
    .Q(d_ff_3_q), .preset(controlled_buffer_1_out), .reset(RESET_out));  // open: clk, D, Qn, en
  D_Flip_Flop #(.trigger("high")) d_ff_4 (
    .clk(clock_1_out), .Q(d_ff_4_q), .preset(RESET_out), .reset(controlled_buffer_1_out));  // open: D, Qn, en
  assign controlled_buffer_1_out = RESET_out ? _3 : 1'bz;  // Controlled_Buffer controlled_buffer_1
  Counter #(.width(3), .max('h7)) counter_1 (
    .load(d_ff_2_q), .D(counter_1_q), .count(d_ff_4_q), .Q(counter_1_q), .clk(clock_1_out));  // open: carry, clr
  LED GAME (.in(d_ff_3_q));
  // Probe on _1
  \ракетка  \u_ракетка_1  (.in_1(_1), .in_2(joystick_1_y));
  Counter #(.width(3), .max('h7)) counter_2 (
    .load(d_ff_1_q), .D(_2), .count(d_ff_4_q), .Q(_2), .clk(clock_1_out));  // open: carry, clr
  Decoder #(.select(3)) decoder_1 (
    .out0(decoder_1_out0[0]), .out1(decoder_1_out0[1]), .out2(decoder_1_out0[2]), .out3(decoder_1_out0[3]),
    .out4(decoder_1_out0[4]), .out5(decoder_1_out0[5]), .out6(decoder_1_out0[6]), .out7(decoder_1_out0[7]),
    .sel(counter_1_q));  // open: en
  DotMatrix #(.matrixcols(8), .matrixrows(8)) dotmatrix_1 (
    .col0(_1), .col1(demultiplexer_1_out1), .col2(demultiplexer_1_out2), .col3(demultiplexer_1_out3),
    .col4(demultiplexer_1_out4), .col5(demultiplexer_1_out5), .col6(demultiplexer_1_out6),
    .col7(demultiplexer_1_out7));
  Demultiplexer #(.select(3), .width(8), .enable("false")) demultiplexer_1 (
    .out1(demultiplexer_1_out1), .out2(demultiplexer_1_out2), .out3(demultiplexer_1_out3),
    .out4(demultiplexer_1_out4), .out5(demultiplexer_1_out5), .out6(demultiplexer_1_out6),
    .out7(demultiplexer_1_out7), .in(decoder_1_out0), .sel(_2));  // open: out0
  and and_5 (and_5_out, decoder_1_out0[0], _1[0]);
  and and_6 (and_6_out, decoder_1_out0[1], _1[1]);
  and and_7 (and_7_out, decoder_1_out0[2], _1[2]);
  and and_8 (and_8_out, decoder_1_out0[3], _1[3]);
  and and_9 (and_9_out, decoder_1_out0[4], _1[4]);
  and and_10 (and_10_out, decoder_1_out0[5], _1[5]);
  and and_11 (and_11_out, decoder_1_out0[6], _1[6]);
  and and_12 (and_12_out, decoder_1_out0[7], _1[7]);
  and \u_Шарик_на_линии_ракетки  (\Шарик_на_линии_ракетки_out , ~_2[0], ~_2[1], ~_2[2]);  // AND_Gate
  and and_13 (_3, \Шарик_на_линии_ракетки_out , ~or_1_out);  // AND_Gate
  or or_1 (or_1_out, and_5_out, and_6_out, and_7_out, and_8_out, and_9_out, and_10_out, and_11_out, and_12_out);
endmodule

module \ракетка  (
  input  [7:0] in_1,
  input  [2:0] in_2
);

  wire decoder_1_out0, decoder_1_out1, decoder_1_out2, decoder_1_out3, decoder_1_out4, decoder_1_out5,
       decoder_1_out6, decoder_1_out7, decoder_1_out8, decoder_1_out9, decoder_1_out10, decoder_1_out11,
       decoder_1_out12, decoder_1_out13, decoder_1_out14, decoder_1_out15, decoder_2_out1, decoder_2_out2,
       decoder_2_out3, decoder_2_out4, decoder_2_out5, decoder_2_out6, decoder_2_out7, decoder_2_out8,
       decoder_2_out9, decoder_2_out10, decoder_2_out11, decoder_2_out12, decoder_2_out13, decoder_2_out14,
       decoder_2_out15, decoder_3_out2, decoder_3_out3, decoder_3_out4, decoder_3_out5, decoder_3_out6,
       decoder_3_out7, decoder_3_out8, decoder_3_out9, decoder_3_out10, decoder_3_out11, decoder_3_out12,
       decoder_3_out13, decoder_3_out14, decoder_3_out15, decoder_4_out0, decoder_4_out1, decoder_4_out2,
       decoder_4_out3, decoder_4_out4, decoder_4_out5, decoder_4_out6, decoder_4_out7, decoder_5_out0,
       decoder_5_out1, decoder_5_out2, decoder_5_out3, decoder_5_out4, decoder_5_out5, decoder_5_out6,
       decoder_5_out7, decoder_6_out0, decoder_6_out1, decoder_6_out2, decoder_6_out3, decoder_6_out4,
       decoder_6_out5, decoder_6_out6, decoder_6_out7, or_3_out, or_4_out;
  wire [3:0] undriven;
  wire [7:0] or_26_out;
  wire [15:0] or_17_out;

  or or_1 (or_17_out[15], decoder_1_out0, decoder_2_out1, decoder_3_out2);
  Decoder #(.select(4)) decoder_1 (
    .out0(decoder_1_out0), .out1(decoder_1_out1), .out2(decoder_1_out2), .out3(decoder_1_out3),
    .out4(decoder_1_out4), .out5(decoder_1_out5), .out6(decoder_1_out6), .out7(decoder_1_out7),
    .out8(decoder_1_out8), .out9(decoder_1_out9), .out10(decoder_1_out10), .out11(decoder_1_out11),
    .out12(decoder_1_out12), .out13(decoder_1_out13), .out14(decoder_1_out14), .out15(decoder_1_out15),
    .sel(undriven));  // open: en
  Decoder #(.select(4)) decoder_2 (
    .out1(decoder_2_out1), .out2(decoder_2_out2), .out3(decoder_2_out3), .out4(decoder_2_out4),
    .out5(decoder_2_out5), .out6(decoder_2_out6), .out7(decoder_2_out7), .out8(decoder_2_out8),
    .out9(decoder_2_out9), .out10(decoder_2_out10), .out11(decoder_2_out11), .out12(decoder_2_out12),
    .out13(decoder_2_out13), .out14(decoder_2_out14), .out15(decoder_2_out15), .sel(undriven));  // open: out0, en
  Decoder #(.select(4)) decoder_3 (
    .out2(decoder_3_out2), .out3(decoder_3_out3), .out4(decoder_3_out4), .out5(decoder_3_out5),
    .out6(decoder_3_out6), .out7(decoder_3_out7), .out8(decoder_3_out8), .out9(decoder_3_out9),
    .out10(decoder_3_out10), .out11(decoder_3_out11), .out12(decoder_3_out12), .out13(decoder_3_out13),
    .out14(decoder_3_out14), .out15(decoder_3_out15), .sel(undriven));  // open: out0, out1, en
  or or_2 (or_17_out[12], decoder_1_out3, decoder_2_out4, decoder_3_out5);
  or or_3 (or_3_out, decoder_1_out1, decoder_2_out2, decoder_3_out3);
  or or_4 (or_4_out, decoder_1_out2, decoder_2_out3, decoder_3_out4);
  or or_5 (or_17_out[11], decoder_1_out4, decoder_2_out5, decoder_3_out6);
  or or_6 (or_17_out[9], decoder_1_out6, decoder_2_out7, decoder_3_out8);
  or or_7 (or_17_out[10], decoder_1_out5, decoder_2_out6, decoder_3_out7);
  or or_8 (or_17_out[7], decoder_1_out8, decoder_2_out9, decoder_3_out10);
  or or_9 (or_17_out[8], decoder_1_out7, decoder_2_out8, decoder_3_out9);
  or or_10 (or_17_out[4], decoder_1_out11, decoder_2_out12, decoder_3_out13);
  or or_11 (or_17_out[6], decoder_1_out9, decoder_2_out10, decoder_3_out11);
  or or_12 (or_17_out[5], decoder_1_out10, decoder_2_out11, decoder_3_out12);
  or or_13 (or_17_out[3], decoder_1_out12, decoder_2_out13, decoder_3_out14);
  or or_14 (or_17_out[2], decoder_1_out13, decoder_2_out14, decoder_3_out15);
  or or_15 (or_17_out[1], decoder_1_out14, decoder_2_out15);
  or or_16 (or_17_out[14], or_17_out[15], or_3_out);
  buf or_17 (or_17_out[0], decoder_1_out15);  // OR_Gate
  or or_18 (or_17_out[13], or_17_out[15], or_4_out);
  Decoder #(.select(3)) decoder_4 (
    .out0(decoder_4_out0), .out1(decoder_4_out1), .out2(decoder_4_out2), .out3(decoder_4_out3),
    .out4(decoder_4_out4), .out5(decoder_4_out5), .out6(decoder_4_out6), .out7(decoder_4_out7), .sel(in_2));  // open: en
  Decoder #(.select(3)) decoder_5 (
    .out0(decoder_5_out0), .out1(decoder_5_out1), .out2(decoder_5_out2), .out3(decoder_5_out3),
    .out4(decoder_5_out4), .out5(decoder_5_out5), .out6(decoder_5_out6), .out7(decoder_5_out7), .sel(in_2));  // open: en
  Decoder #(.select(3)) decoder_6 (
    .out0(decoder_6_out0), .out1(decoder_6_out1), .out2(decoder_6_out2), .out3(decoder_6_out3),
    .out4(decoder_6_out4), .out5(decoder_6_out5), .out6(decoder_6_out6), .out7(decoder_6_out7), .sel(in_2));  // open: en
  or or_19 (or_26_out[7], decoder_4_out0, decoder_5_out0, decoder_6_out0);
  or or_20 (or_26_out[6], decoder_4_out1, decoder_5_out1, decoder_6_out1);
  or or_21 (or_26_out[5], decoder_4_out2, decoder_5_out2, decoder_6_out2);
  or or_22 (or_26_out[4], decoder_4_out3, decoder_5_out3, decoder_6_out3);
  or or_23 (or_26_out[3], decoder_4_out4, decoder_5_out4, decoder_6_out4);
  or or_24 (or_26_out[2], decoder_4_out5, decoder_5_out5, decoder_6_out5);
  or or_25 (or_26_out[1], decoder_4_out6, decoder_5_out6, decoder_6_out6);
  or or_26 (or_26_out[0], decoder_4_out7, decoder_5_out7, decoder_6_out7);
endmodule

module _11 (
  input  [7:0] in_1,
  input  [7:0] in_2
);

  // DotMatrix #(.inputtype("select"), .matrixcols(8), .matrixrows(8)) dotmatrix_1: pin names not known; wires that end beside it: in_1, in_2
endmodule
