// Logisim project pong .circ as structural Verilog: 4 circuits, main circuit main
module main (
  output [15:0] out_1,
  output [15:0] out_2
);

  wire and_1_out, and_2_out, and_4_out, and_5_out, and_7_out, and_8_out, and_10_out, and_11_out, and_12_out,
       clk_ball_out, clk_board_out, collision_det_1_match, comparator_1_eq, comparator_2_eq, d_ff_1_q,
       d_ff_2_q, d_ff_3_q, d_ff_4_q, d_ff_5_q, d_ff_6_q, d_ff_7_q, d_ff_8_q, d_ff_9_q, d_ff_10_q, d_ff_11_q,
       nor_1_out, nor_2_out, nor_3_out, not_1_out, not_2_out, not_3_out, or_1_out, or_2_out, or_4_out,
       or_6_out, start_out, \Лево_out , \Право_out ;
  wire [1:0] joystick_1_y;
  wire [3:0] adder_1_out, adder_2_out, adder_3_out, adder_4_out, counter_1_q, multiplexer_1_out,
       multiplexer_2_out, or_3_out, or_5_out, register_1_q, register_2_q, register_3_q;
  wire [3:3] and_6_out;
  wire [15:0] ball_decoder_1_out_4, ball_decoder_1_out_5, ball_decoder_1_out_6, ball_decoder_1_out_7,
       ball_decoder_1_out_8, ball_decoder_1_out_9, ball_decoder_1_out_10, ball_decoder_1_out_11,
       ball_decoder_1_out_12, ball_decoder_1_out_13, ball_decoder_1_out_14, ball_decoder_1_out_15,
       ball_decoder_1_out_16, ball_decoder_1_out_17, ball_decoder_1_out_18, ball_decoder_1_out_19, xor_1_out;

  Button \u_Право  (.out(\Право_out ));
  Button \u_Лево  (.out(\Лево_out ));
  Joystick #(.bits(2)) joystick_1 (.y(joystick_1_y));  // open: x
  Button start (.out(start_out));
  D_Flip_Flop d_ff_1 (.Q(d_ff_1_q), .preset(or_4_out), .reset(and_7_out));  // open: clk, D, Qn, en
  and and_1 (and_1_out, ~joystick_1_y[1], joystick_1_y[0]);  // AND_Gate
  or or_1 (or_1_out, and_1_out, \Право_out );
  or or_2 (or_2_out, \Лево_out , and_2_out);
  and and_2 (and_2_out, joystick_1_y[1], joystick_1_y[0]);
  and and_3 (or_3_out[3], ~d_ff_1_q, d_ff_7_q);  // AND_Gate
  and and_4 (and_4_out, d_ff_7_q, d_ff_1_q);
  and and_5 (and_5_out, ~comparator_1_eq, or_1_out, ~and_6_out[3]);  // AND_Gate
  and and_6 (and_6_out[3], ~and_5_out, or_2_out, ~comparator_2_eq);  // AND_Gate
  Clock clk_board (.out(clk_board_out));
  or or_3 (or_3_out[0], or_3_out[3], and_4_out);
  Adder #(.width(4)) adder_1 (
    .a(register_1_q), .b({4{and_6_out[3]}}), .out(adder_1_out), .cin(and_5_out));  // open: cout
  Multiplexer #(.width(4), .disabled(0), .enable("false")) multiplexer_1 (
    .in0(4'b1111), .in1(adder_2_out), .out(multiplexer_1_out), .sel(d_ff_7_q));
  Adder #(.width(4)) adder_2 (
    .a(register_2_q), .b({{3{or_3_out[3]}}, or_3_out[0]}), .out(adder_2_out));  // open: cin, cout
  Register #(.width(4)) register_1 (.D(adder_1_out), .Q(register_1_q), .clk(clk_board_out));  // open: en, clr
  Register #(.width(4)) register_2 (
    .D(multiplexer_1_out), .Q(register_2_q), .clk(or_6_out), .clr(d_ff_4_q));  // open: en
  b_shift_16b b_shift_16b_1 (.in_1(16'hf), .shift(adder_3_out), .out_3(out_2));
  Comparator #(.width(4), .mode("unsigned")) comparator_1 (
    .a(4'b1100), .b(adder_3_out), .eq(comparator_1_eq));  // open: gt, lt
  Adder #(.width(4)) adder_3 (.a(register_1_q), .b(4'b0110), .out(adder_3_out));  // open: cin, cout
  and and_7 (and_7_out, register_2_q[3], register_2_q[2], register_2_q[1], register_2_q[0]);
  nor nor_1 (nor_1_out, register_2_q[3], register_2_q[2], register_2_q[1], register_2_q[0]);
  or or_4 (or_4_out, nor_1_out, d_ff_3_q, d_ff_4_q);
  Comparator #(.width(4), .mode("unsigned")) comparator_2 (
    .a(adder_3_out), .b(4'b0000), .eq(comparator_2_eq));  // open: gt, lt
  collision_det collision_det_1 (
    .board_pos(adder_3_out), .Y_direction__1_plus(d_ff_6_q), .ball_Y(register_3_q), .ball_X_1(nor_2_out),
    .match(collision_det_1_match));
  nor nor_2 (nor_2_out, d_ff_1_q, register_2_q[3], register_2_q[2], register_2_q[1], ~register_2_q[0]);  // NOR_Gate
  and and_8 (and_8_out, nor_2_out, ~collision_det_1_match);  // AND_Gate
  assign xor_1_out = out_2 ^ ball_decoder_1_out_4;  // XOR_Gate xor_1, 16 bits wide
  D_Flip_Flop d_ff_2 (.clk(clk_ball_out), .D(collision_det_1_match), .Q(d_ff_2_q));  // open: Qn, preset, en, reset
  D_Flip_Flop #(.trigger("falling")) d_ff_3 (
    .clk(clk_ball_out), .D(and_8_out), .Q(d_ff_3_q));  // open: Qn, preset, en, reset
  ball_decoder ball_decoder_1 (
    .pos_Y(register_3_q), .pos_X(register_2_q), .ball_en(d_ff_7_q), .out_4(ball_decoder_1_out_4),
    .out_5(ball_decoder_1_out_5), .out_6(ball_decoder_1_out_6), .out_7(ball_decoder_1_out_7),
    .out_8(ball_decoder_1_out_8), .out_9(ball_decoder_1_out_9), .out_10(ball_decoder_1_out_10),
    .out_11(ball_decoder_1_out_11), .out_12(ball_decoder_1_out_12), .out_13(ball_decoder_1_out_13),
    .out_14(ball_decoder_1_out_14), .out_15(ball_decoder_1_out_15), .out_16(ball_decoder_1_out_16),
    .out_17(ball_decoder_1_out_17), .out_18(ball_decoder_1_out_18), .out_19(ball_decoder_1_out_19));
  D_Flip_Flop d_ff_4 (.clk(clk_ball_out), .D(d_ff_2_q), .Q(d_ff_4_q));  // open: Qn, preset, en, reset
  Clock #(.highDuration(2), .lowDuration(2)) clk_ball (.out(clk_ball_out));
  D_Flip_Flop d_ff_5 (.clk(start_out), .D(1'b0), .Q(d_ff_5_q), .preset(d_ff_4_q));  // open: Qn, en, reset
  DotMatrix #(.inputtype("row"), .matrixcols(16), .matrixrows(16)) dotmatrix_1 (
    .row0(ball_decoder_1_out_19), .row1(ball_decoder_1_out_18), .row2(ball_decoder_1_out_17),
    .row3(ball_decoder_1_out_16), .row4(ball_decoder_1_out_15), .row5(ball_decoder_1_out_14),
    .row6(ball_decoder_1_out_13), .row7(ball_decoder_1_out_12), .row8(ball_decoder_1_out_11),
    .row9(ball_decoder_1_out_10), .row10(ball_decoder_1_out_9), .row11(ball_decoder_1_out_8),
    .row12(ball_decoder_1_out_7), .row13(ball_decoder_1_out_6), .row14(ball_decoder_1_out_5),
    .row15(xor_1_out));
  LED lost_ball (.in(d_ff_5_q));
  D_Flip_Flop d_ff_6 (.Q(d_ff_6_q), .preset(nor_3_out), .reset(and_12_out));  // open: clk, D, Qn, en
  and and_9 (or_5_out[3], ~d_ff_6_q, d_ff_7_q);  // AND_Gate
  and and_10 (and_10_out, d_ff_7_q, d_ff_6_q);
  or or_5 (or_5_out[0], or_5_out[3], and_10_out);
  Counter #(.width(4), .max('hf)) counter_1 (.Q(counter_1_q), .clk(clk_ball_out));  // open: load, D, count, carry, clr
  D_Flip_Flop d_ff_7 (.clk(start_out), .D(1'b1), .Q(d_ff_7_q), .en(d_ff_10_q), .reset(d_ff_4_q));  // open: Qn, preset
  not not_1 (not_1_out, d_ff_7_q);
  not not_2 (not_2_out, d_ff_11_q);
  D_Flip_Flop d_ff_8 (.clk(d_ff_11_q), .D(1'b1), .Q(d_ff_8_q), .reset(d_ff_4_q));  // open: Qn, preset, en
  Multiplexer #(.width(4), .disabled(0), .enable("false")) multiplexer_2 (
    .in0(counter_1_q), .in1(adder_4_out), .out(multiplexer_2_out), .sel(d_ff_7_q));
  Adder #(.width(4)) adder_4 (
    .a(register_3_q), .b({{3{or_5_out[3]}}, or_5_out[0]}), .out(adder_4_out));  // open: cin, cout
  and and_11 (and_11_out, d_ff_7_q, clk_ball_out);
  D_Flip_Flop d_ff_9 (.clk(clk_ball_out), .D(not_1_out), .Q(d_ff_9_q), .en(not_2_out));  // open: Qn, preset, reset
  not not_3 (not_3_out, d_ff_8_q);
  D_Flip_Flop d_ff_10 (.clk(clk_ball_out), .D(d_ff_8_q), .Q(d_ff_10_q));  // open: Qn, preset, en, reset
  Register #(.width(4)) register_3 (.D(multiplexer_2_out), .Q(register_3_q), .clk(or_6_out));  // open: en, clr
  or or_6 (or_6_out, and_11_out, d_ff_11_q);
  D_Flip_Flop d_ff_11 (
    .clk(clk_ball_out), .D(d_ff_9_q), .Q(d_ff_11_q), .en(not_3_out), .reset(d_ff_10_q));  // open: Qn, preset
  and and_12 (and_12_out, register_3_q[3], register_3_q[2], register_3_q[1], register_3_q[0]);
  nor nor_3 (nor_3_out, register_3_q[3], register_3_q[2], register_3_q[1], register_3_q[0]);

  assign out_1 = 16'hf;

  // Notes on the sheet:
  //   X-driver
  //   board-driver
  //   Y-driver
  //   INIT
endmodule

// >>
module b_shift_16b (
  input  [15:0] in_1,
  input  [3:0] shift,
  output [15:0] out_3
);

  wire multiplexer_1_out, multiplexer_2_out, multiplexer_3_out, multiplexer_4_out, multiplexer_5_out,
       multiplexer_6_out, multiplexer_7_out, multiplexer_8_out, multiplexer_9_out, multiplexer_10_out,
       multiplexer_11_out, multiplexer_12_out, multiplexer_13_out, multiplexer_14_out, multiplexer_15_out,
       multiplexer_16_out, multiplexer_17_out, multiplexer_18_out, multiplexer_19_out, multiplexer_20_out,
       multiplexer_21_out, multiplexer_22_out, multiplexer_23_out, multiplexer_24_out, multiplexer_25_out,
       multiplexer_26_out, multiplexer_27_out, multiplexer_28_out, multiplexer_29_out, multiplexer_30_out,
       multiplexer_31_out, multiplexer_32_out, multiplexer_33_out, multiplexer_34_out, multiplexer_35_out,
       multiplexer_36_out, multiplexer_37_out, multiplexer_38_out, multiplexer_39_out, multiplexer_40_out,
       multiplexer_41_out, multiplexer_42_out, multiplexer_43_out, multiplexer_44_out, multiplexer_45_out,
       multiplexer_46_out, multiplexer_47_out, multiplexer_48_out;

  Multiplexer #(.disabled(0), .enable("false")) multiplexer_1 (
    .in0(in_1[0]), .in1(1'b0), .out(multiplexer_1_out), .sel(shift[0]));
  Multiplexer #(.disabled(0), .enable("false")) multiplexer_2 (
    .in0(in_1[1]), .in1(in_1[0]), .out(multiplexer_2_out), .sel(shift[0]));
  Multiplexer #(.disabled(0), .enable("false")) multiplexer_3 (
    .in0(in_1[2]), .in1(in_1[1]), .out(multiplexer_3_out), .sel(shift[0]));
  Multiplexer #(.disabled(0), .enable("false")) multiplexer_4 (
    .in0(in_1[3]), .in1(in_1[2]), .out(multiplexer_4_out), .sel(shift[0]));
  Multiplexer #(.disabled(0), .enable("false")) multiplexer_5 (
    .in0(in_1[4]), .in1(in_1[3]), .out(multiplexer_5_out), .sel(shift[0]));
  Multiplexer #(.disabled(0), .enable("false")) multiplexer_6 (
    .in0(in_1[5]), .in1(in_1[4]), .out(multiplexer_6_out), .sel(shift[0]));
  Multiplexer #(.disabled(0), .enable("false")) multiplexer_7 (
    .in0(in_1[6]), .in1(in_1[5]), .out(multiplexer_7_out), .sel(shift[0]));
  Multiplexer #(.disabled(0), .enable("false")) multiplexer_8 (
    .in0(in_1[7]), .in1(in_1[6]), .out(multiplexer_8_out), .sel(shift[0]));
  Multiplexer #(.disabled(0), .enable("false")) multiplexer_9 (
    .in0(in_1[8]), .in1(in_1[7]), .out(multiplexer_9_out), .sel(shift[0]));
  Multiplexer #(.disabled(0), .enable("false")) multiplexer_10 (
    .in0(in_1[9]), .in1(in_1[8]), .out(multiplexer_10_out), .sel(shift[0]));
  Multiplexer #(.disabled(0), .enable("false")) multiplexer_11 (
    .in0(in_1[10]), .in1(in_1[9]), .out(multiplexer_11_out), .sel(shift[0]));
  Multiplexer #(.disabled(0), .enable("false")) multiplexer_12 (
    .in0(in_1[11]), .in1(in_1[10]), .out(multiplexer_12_out), .sel(shift[0]));
  Multiplexer #(.disabled(0), .enable("false")) multiplexer_13 (
    .in0(in_1[12]), .in1(in_1[11]), .out(multiplexer_13_out), .sel(shift[0]));
  Multiplexer #(.disabled(0), .enable("false")) multiplexer_14 (
    .in0(in_1[13]), .in1(in_1[12]), .out(multiplexer_14_out), .sel(shift[0]));
  Multiplexer #(.disabled(0), .enable("false")) multiplexer_15 (
    .in0(in_1[14]), .in1(in_1[13]), .out(multiplexer_15_out), .sel(shift[0]));
  Multiplexer #(.disabled(0), .enable("false")) multiplexer_16 (
    .in0(in_1[15]), .in1(in_1[14]), .out(multiplexer_16_out), .sel(shift[0]));
  Multiplexer #(.disabled(0), .enable("false")) multiplexer_17 (
    .in0(multiplexer_1_out), .in1(1'b0), .out(multiplexer_17_out), .sel(shift[1]));
  Multiplexer #(.disabled(0), .enable("false")) multiplexer_18 (
    .in0(multiplexer_2_out), .in1(1'b0), .out(multiplexer_18_out), .sel(shift[1]));
  Multiplexer #(.disabled(0), .enable("false")) multiplexer_19 (
    .in0(multiplexer_3_out), .in1(multiplexer_1_out), .out(multiplexer_19_out), .sel(shift[1]));
  Multiplexer #(.disabled(0), .enable("false")) multiplexer_20 (
    .in0(multiplexer_4_out), .in1(multiplexer_2_out), .out(multiplexer_20_out), .sel(shift[1]));
  Multiplexer #(.disabled(0), .enable("false")) multiplexer_21 (
    .in0(multiplexer_5_out), .in1(multiplexer_3_out), .out(multiplexer_21_out), .sel(shift[1]));
  Multiplexer #(.disabled(0), .enable("false")) multiplexer_22 (
    .in0(multiplexer_6_out), .in1(multiplexer_4_out), .out(multiplexer_22_out), .sel(shift[1]));
  Multiplexer #(.disabled(0), .enable("false")) multiplexer_23 (
    .in0(multiplexer_7_out), .in1(multiplexer_5_out), .out(multiplexer_23_out), .sel(shift[1]));
  Multiplexer #(.disabled(0), .enable("false")) multiplexer_24 (
    .in0(multiplexer_8_out), .in1(multiplexer_6_out), .out(multiplexer_24_out), .sel(shift[1]));
  Multiplexer #(.disabled(0), .enable("false")) multiplexer_25 (
    .in0(multiplexer_9_out), .in1(multiplexer_7_out), .out(multiplexer_25_out), .sel(shift[1]));
  Multiplexer #(.disabled(0), .enable("false")) multiplexer_26 (
    .in0(multiplexer_10_out), .in1(multiplexer_8_out), .out(multiplexer_26_out), .sel(shift[1]));
  Multiplexer #(.disabled(0), .enable("false")) multiplexer_27 (
    .in0(multiplexer_11_out), .in1(multiplexer_9_out), .out(multiplexer_27_out), .sel(shift[1]));
  Multiplexer #(.disabled(0), .enable("false")) multiplexer_28 (
    .in0(multiplexer_12_out), .in1(multiplexer_10_out), .out(multiplexer_28_out), .sel(shift[1]));
  Multiplexer #(.disabled(0), .enable("false")) multiplexer_29 (
    .in0(multiplexer_13_out), .in1(multiplexer_11_out), .out(multiplexer_29_out), .sel(shift[1]));
  Multiplexer #(.disabled(0), .enable("false")) multiplexer_30 (
    .in0(multiplexer_14_out), .in1(multiplexer_12_out), .out(multiplexer_30_out), .sel(shift[1]));
  Multiplexer #(.disabled(0), .enable("false")) multiplexer_31 (
    .in0(multiplexer_15_out), .in1(multiplexer_13_out), .out(multiplexer_31_out), .sel(shift[1]));
  Multiplexer #(.disabled(0), .enable("false")) multiplexer_32 (
    .in0(multiplexer_16_out), .in1(multiplexer_14_out), .out(multiplexer_32_out), .sel(shift[1]));
  Multiplexer #(.disabled(0), .enable("false")) multiplexer_33 (
    .in0(multiplexer_17_out), .in1(1'b0), .out(multiplexer_33_out), .sel(shift[2]));
  Multiplexer #(.disabled(0), .enable("false")) multiplexer_34 (
    .in0(multiplexer_18_out), .in1(1'b0), .out(multiplexer_34_out), .sel(shift[2]));
  Multiplexer #(.disabled(0), .enable("false")) multiplexer_35 (
    .in0(multiplexer_19_out), .in1(1'b0), .out(multiplexer_35_out), .sel(shift[2]));
  Multiplexer #(.disabled(0), .enable("false")) multiplexer_36 (
    .in0(multiplexer_20_out), .in1(1'b0), .out(multiplexer_36_out), .sel(shift[2]));
  Multiplexer #(.disabled(0), .enable("false")) multiplexer_37 (
    .in0(multiplexer_21_out), .in1(multiplexer_17_out), .out(multiplexer_37_out), .sel(shift[2]));
  Multiplexer #(.disabled(0), .enable("false")) multiplexer_38 (
    .in0(multiplexer_22_out), .in1(multiplexer_18_out), .out(multiplexer_38_out), .sel(shift[2]));
  Multiplexer #(.disabled(0), .enable("false")) multiplexer_39 (
    .in0(multiplexer_23_out), .in1(multiplexer_19_out), .out(multiplexer_39_out), .sel(shift[2]));
  Multiplexer #(.disabled(0), .enable("false")) multiplexer_40 (
    .in0(multiplexer_24_out), .in1(multiplexer_20_out), .out(multiplexer_40_out), .sel(shift[2]));
  Multiplexer #(.disabled(0), .enable("false")) multiplexer_41 (
    .in0(multiplexer_25_out), .in1(multiplexer_21_out), .out(multiplexer_41_out), .sel(shift[2]));
  Multiplexer #(.disabled(0), .enable("false")) multiplexer_42 (
    .in0(multiplexer_26_out), .in1(multiplexer_22_out), .out(multiplexer_42_out), .sel(shift[2]));
  Multiplexer #(.disabled(0), .enable("false")) multiplexer_43 (
    .in0(multiplexer_27_out), .in1(multiplexer_23_out), .out(multiplexer_43_out), .sel(shift[2]));
  Multiplexer #(.disabled(0), .enable("false")) multiplexer_44 (
    .in0(multiplexer_28_out), .in1(multiplexer_24_out), .out(multiplexer_44_out), .sel(shift[2]));
  Multiplexer #(.disabled(0), .enable("false")) multiplexer_45 (
    .in0(multiplexer_29_out), .in1(multiplexer_25_out), .out(multiplexer_45_out), .sel(shift[2]));
  Multiplexer #(.disabled(0), .enable("false")) multiplexer_46 (
    .in0(multiplexer_30_out), .in1(multiplexer_26_out), .out(multiplexer_46_out), .sel(shift[2]));
  Multiplexer #(.disabled(0), .enable("false")) multiplexer_47 (
    .in0(multiplexer_31_out), .in1(multiplexer_27_out), .out(multiplexer_47_out), .sel(shift[2]));
  Multiplexer #(.disabled(0), .enable("false")) multiplexer_48 (
    .in0(multiplexer_32_out), .in1(multiplexer_28_out), .out(multiplexer_48_out), .sel(shift[2]));
  Multiplexer #(.disabled(0), .enable("false")) multiplexer_49 (
    .in0(multiplexer_33_out), .in1(1'b0), .out(out_3[0]), .sel(shift[3]));
  Multiplexer #(.disabled(0), .enable("false")) multiplexer_50 (
    .in0(multiplexer_34_out), .in1(1'b0), .out(out_3[1]), .sel(shift[3]));
  Multiplexer #(.disabled(0), .enable("false")) multiplexer_51 (
    .in0(multiplexer_35_out), .in1(1'b0), .out(out_3[2]), .sel(shift[3]));
  Multiplexer #(.disabled(0), .enable("false")) multiplexer_52 (
    .in0(multiplexer_36_out), .in1(1'b0), .out(out_3[3]), .sel(shift[3]));
  Multiplexer #(.disabled(0), .enable("false")) multiplexer_53 (
    .in0(multiplexer_37_out), .in1(1'b0), .out(out_3[4]), .sel(shift[3]));
  Multiplexer #(.disabled(0), .enable("false")) multiplexer_54 (
    .in0(multiplexer_38_out), .in1(1'b0), .out(out_3[5]), .sel(shift[3]));
  Multiplexer #(.disabled(0), .enable("false")) multiplexer_55 (
    .in0(multiplexer_39_out), .in1(1'b0), .out(out_3[6]), .sel(shift[3]));
  Multiplexer #(.disabled(0), .enable("false")) multiplexer_56 (
    .in0(multiplexer_40_out), .in1(1'b0), .out(out_3[7]), .sel(shift[3]));
  Multiplexer #(.disabled(0), .enable("false")) multiplexer_57 (
    .in0(multiplexer_41_out), .in1(multiplexer_33_out), .out(out_3[8]), .sel(shift[3]));
  Multiplexer #(.disabled(0), .enable("false")) multiplexer_58 (
    .in0(multiplexer_42_out), .in1(multiplexer_34_out), .out(out_3[9]), .sel(shift[3]));
  Multiplexer #(.disabled(0), .enable("false")) multiplexer_59 (
    .in0(multiplexer_43_out), .in1(multiplexer_35_out), .out(out_3[10]), .sel(shift[3]));
  Multiplexer #(.disabled(0), .enable("false")) multiplexer_60 (
    .in0(multiplexer_44_out), .in1(multiplexer_36_out), .out(out_3[11]), .sel(shift[3]));
  Multiplexer #(.disabled(0), .enable("false")) multiplexer_61 (
    .in0(multiplexer_45_out), .in1(multiplexer_37_out), .out(out_3[12]), .sel(shift[3]));
  Multiplexer #(.disabled(0), .enable("false")) multiplexer_62 (
    .in0(multiplexer_46_out), .in1(multiplexer_38_out), .out(out_3[13]), .sel(shift[3]));
  Multiplexer #(.disabled(0), .enable("false")) multiplexer_63 (
    .in0(multiplexer_47_out), .in1(multiplexer_39_out), .out(out_3[14]), .sel(shift[3]));
  Multiplexer #(.disabled(0), .enable("false")) multiplexer_64 (
    .in0(multiplexer_48_out), .in1(multiplexer_40_out), .out(out_3[15]), .sel(shift[3]));
endmodule

module ball_decoder (
  input  [3:0] pos_Y,
  input  [3:0] pos_X,
  input  ball_en,
  output [15:0] out_4,
  output [15:0] out_5,
  output [15:0] out_6,
  output [15:0] out_7,
  output [15:0] out_8,
  output [15:0] out_9,
  output [15:0] out_10,
  output [15:0] out_11,
  output [15:0] out_12,
  output [15:0] out_13,
  output [15:0] out_14,
  output [15:0] out_15,
  output [15:0] out_16,
  output [15:0] out_17,
  output [15:0] out_18,
  output [15:0] out_19
);

  wire decoder_2_out0, decoder_2_out1, decoder_2_out2, decoder_2_out3, decoder_2_out4, decoder_2_out5,
       decoder_2_out6, decoder_2_out7, decoder_2_out8, decoder_2_out9, decoder_2_out10, decoder_2_out11,
       decoder_2_out12, decoder_2_out13, decoder_2_out14, decoder_2_out15;

  Decoder #(.select(4), .disabled(0)) decoder_1 (
    .out0(out_4[0]), .out1(out_4[1]), .out2(out_4[2]), .out3(out_4[3]), .out4(out_4[4]), .out5(out_4[5]),
    .out6(out_4[6]), .out7(out_4[7]), .out8(out_4[8]), .out9(out_4[9]), .out10(out_4[10]), .out11(out_4[11]),
    .out12(out_4[12]), .out13(out_4[13]), .out14(out_4[14]), .out15(out_4[15]), .sel(pos_Y),
    .en(decoder_2_out0));
  Decoder #(.select(4), .disabled(0)) decoder_2 (
    .out0(decoder_2_out0), .out1(decoder_2_out1), .out2(decoder_2_out2), .out3(decoder_2_out3),
    .out4(decoder_2_out4), .out5(decoder_2_out5), .out6(decoder_2_out6), .out7(decoder_2_out7),
    .out8(decoder_2_out8), .out9(decoder_2_out9), .out10(decoder_2_out10), .out11(decoder_2_out11),
    .out12(decoder_2_out12), .out13(decoder_2_out13), .out14(decoder_2_out14), .out15(decoder_2_out15),
    .sel(pos_X), .en(ball_en));
  Decoder #(.select(4), .disabled(0)) decoder_3 (
    .out0(out_5[0]), .out1(out_5[1]), .out2(out_5[2]), .out3(out_5[3]), .out4(out_5[4]), .out5(out_5[5]),
    .out6(out_5[6]), .out7(out_5[7]), .out8(out_5[8]), .out9(out_5[9]), .out10(out_5[10]), .out11(out_5[11]),
    .out12(out_5[12]), .out13(out_5[13]), .out14(out_5[14]), .out15(out_5[15]), .sel(pos_Y),
    .en(decoder_2_out1));
  Decoder #(.select(4), .disabled(0)) decoder_4 (
    .out0(out_6[0]), .out1(out_6[1]), .out2(out_6[2]), .out3(out_6[3]), .out4(out_6[4]), .out5(out_6[5]),
    .out6(out_6[6]), .out7(out_6[7]), .out8(out_6[8]), .out9(out_6[9]), .out10(out_6[10]), .out11(out_6[11]),
    .out12(out_6[12]), .out13(out_6[13]), .out14(out_6[14]), .out15(out_6[15]), .sel(pos_Y),
    .en(decoder_2_out2));
  Decoder #(.select(4), .disabled(0)) decoder_5 (
    .out0(out_7[0]), .out1(out_7[1]), .out2(out_7[2]), .out3(out_7[3]), .out4(out_7[4]), .out5(out_7[5]),
    .out6(out_7[6]), .out7(out_7[7]), .out8(out_7[8]), .out9(out_7[9]), .out10(out_7[10]), .out11(out_7[11]),
    .out12(out_7[12]), .out13(out_7[13]), .out14(out_7[14]), .out15(out_7[15]), .sel(pos_Y),
    .en(decoder_2_out3));
  Decoder #(.select(4), .disabled(0)) decoder_6 (
    .out0(out_8[0]), .out1(out_8[1]), .out2(out_8[2]), .out3(out_8[3]), .out4(out_8[4]), .out5(out_8[5]),
    .out6(out_8[6]), .out7(out_8[7]), .out8(out_8[8]), .out9(out_8[9]), .out10(out_8[10]), .out11(out_8[11]),
    .out12(out_8[12]), .out13(out_8[13]), .out14(out_8[14]), .out15(out_8[15]), .sel(pos_Y),
    .en(decoder_2_out4));
  Decoder #(.select(4), .disabled(0)) decoder_7 (
    .out0(out_9[0]), .out1(out_9[1]), .out2(out_9[2]), .out3(out_9[3]), .out4(out_9[4]), .out5(out_9[5]),
    .out6(out_9[6]), .out7(out_9[7]), .out8(out_9[8]), .out9(out_9[9]), .out10(out_9[10]), .out11(out_9[11]),
    .out12(out_9[12]), .out13(out_9[13]), .out14(out_9[14]), .out15(out_9[15]), .sel(pos_Y),
    .en(decoder_2_out5));
  Decoder #(.select(4), .disabled(0)) decoder_8 (
    .out0(out_10[0]), .out1(out_10[1]), .out2(out_10[2]), .out3(out_10[3]), .out4(out_10[4]),
    .out5(out_10[5]), .out6(out_10[6]), .out7(out_10[7]), .out8(out_10[8]), .out9(out_10[9]),
    .out10(out_10[10]), .out11(out_10[11]), .out12(out_10[12]), .out13(out_10[13]), .out14(out_10[14]),
    .out15(out_10[15]), .sel(pos_Y), .en(decoder_2_out6));
  Decoder #(.select(4), .disabled(0)) decoder_9 (
    .out0(out_11[0]), .out1(out_11[1]), .out2(out_11[2]), .out3(out_11[3]), .out4(out_11[4]),
    .out5(out_11[5]), .out6(out_11[6]), .out7(out_11[7]), .out8(out_11[8]), .out9(out_11[9]),
    .out10(out_11[10]), .out11(out_11[11]), .out12(out_11[12]), .out13(out_11[13]), .out14(out_11[14]),
    .out15(out_11[15]), .sel(pos_Y), .en(decoder_2_out7));
  Decoder #(.select(4), .disabled(0)) decoder_10 (
    .out0(out_12[0]), .out1(out_12[1]), .out2(out_12[2]), .out3(out_12[3]), .out4(out_12[4]),
    .out5(out_12[5]), .out6(out_12[6]), .out7(out_12[7]), .out8(out_12[8]), .out9(out_12[9]),
    .out10(out_12[10]), .out11(out_12[11]), .out12(out_12[12]), .out13(out_12[13]), .out14(out_12[14]),
    .out15(out_12[15]), .sel(pos_Y), .en(decoder_2_out8));
  Decoder #(.select(4), .disabled(0)) decoder_11 (
    .out0(out_13[0]), .out1(out_13[1]), .out2(out_13[2]), .out3(out_13[3]), .out4(out_13[4]),
    .out5(out_13[5]), .out6(out_13[6]), .out7(out_13[7]), .out8(out_13[8]), .out9(out_13[9]),
    .out10(out_13[10]), .out11(out_13[11]), .out12(out_13[12]), .out13(out_13[13]), .out14(out_13[14]),
    .out15(out_13[15]), .sel(pos_Y), .en(decoder_2_out9));
  Decoder #(.select(4), .disabled(0)) decoder_12 (
    .out0(out_14[0]), .out1(out_14[1]), .out2(out_14[2]), .out3(out_14[3]), .out4(out_14[4]),
    .out5(out_14[5]), .out6(out_14[6]), .out7(out_14[7]), .out8(out_14[8]), .out9(out_14[9]),
    .out10(out_14[10]), .out11(out_14[11]), .out12(out_14[12]), .out13(out_14[13]), .out14(out_14[14]),
    .out15(out_14[15]), .sel(pos_Y), .en(decoder_2_out10));
  Decoder #(.select(4), .disabled(0)) decoder_13 (
    .out0(out_15[0]), .out1(out_15[1]), .out2(out_15[2]), .out3(out_15[3]), .out4(out_15[4]),
    .out5(out_15[5]), .out6(out_15[6]), .out7(out_15[7]), .out8(out_15[8]), .out9(out_15[9]),
    .out10(out_15[10]), .out11(out_15[11]), .out12(out_15[12]), .out13(out_15[13]), .out14(out_15[14]),
    .out15(out_15[15]), .sel(pos_Y), .en(decoder_2_out11));
  Decoder #(.select(4), .disabled(0)) decoder_14 (
    .out0(out_16[0]), .out1(out_16[1]), .out2(out_16[2]), .out3(out_16[3]), .out4(out_16[4]),
    .out5(out_16[5]), .out6(out_16[6]), .out7(out_16[7]), .out8(out_16[8]), .out9(out_16[9]),
    .out10(out_16[10]), .out11(out_16[11]), .out12(out_16[12]), .out13(out_16[13]), .out14(out_16[14]),
    .out15(out_16[15]), .sel(pos_Y), .en(decoder_2_out12));
  Decoder #(.select(4), .disabled(0)) decoder_15 (
    .out0(out_17[0]), .out1(out_17[1]), .out2(out_17[2]), .out3(out_17[3]), .out4(out_17[4]),
    .out5(out_17[5]), .out6(out_17[6]), .out7(out_17[7]), .out8(out_17[8]), .out9(out_17[9]),
    .out10(out_17[10]), .out11(out_17[11]), .out12(out_17[12]), .out13(out_17[13]), .out14(out_17[14]),
    .out15(out_17[15]), .sel(pos_Y), .en(decoder_2_out13));
  Decoder #(.select(4), .disabled(0)) decoder_16 (
    .out0(out_18[0]), .out1(out_18[1]), .out2(out_18[2]), .out3(out_18[3]), .out4(out_18[4]),
    .out5(out_18[5]), .out6(out_18[6]), .out7(out_18[7]), .out8(out_18[8]), .out9(out_18[9]),
    .out10(out_18[10]), .out11(out_18[11]), .out12(out_18[12]), .out13(out_18[13]), .out14(out_18[14]),
    .out15(out_18[15]), .sel(pos_Y), .en(decoder_2_out14));
  Decoder #(.select(4), .disabled(0)) decoder_17 (
    .out0(out_19[0]), .out1(out_19[1]), .out2(out_19[2]), .out3(out_19[3]), .out4(out_19[4]),
    .out5(out_19[5]), .out6(out_19[6]), .out7(out_19[7]), .out8(out_19[8]), .out9(out_19[9]),
    .out10(out_19[10]), .out11(out_19[11]), .out12(out_19[12]), .out13(out_19[13]), .out14(out_19[14]),
    .out15(out_19[15]), .sel(pos_Y), .en(decoder_2_out15));
endmodule

// col
module collision_det (
  input  [3:0] board_pos,
  input  Y_direction__1_plus,
  input  [3:0] ball_Y,
  input  ball_X_1,
  output match
);

  wire and_1_out, and_2_out, and_3_out, and_5_out, and_6_out, and_7_out, comparator_1_eq, comparator_1_gt,
       comparator_2_eq, comparator_2_lt, nor_1_out, nor_2_out, or_1_out, or_2_out, or_3_out;
  wire [3:0] adder_1_out, adder_2_out;
  wire [3:3] and_4_out;

  // Probe on board_pos
  // Probe on ball_Y
  // Probe on adder_1_out
  Adder #(.width(4)) adder_1 (.a(4'b0011), .b(board_pos), .out(adder_1_out));  // open: cin, cout
  and and_1 (and_1_out, board_pos[3], board_pos[2], ~board_pos[1], ~board_pos[0]);  // AND_Gate
  nor nor_1 (nor_1_out, board_pos[3], board_pos[2], board_pos[1], board_pos[0]);
  and and_2 (and_2_out, nor_1_out, nor_2_out);
  nor nor_2 (nor_2_out, ball_Y[0], ball_Y[1], ball_Y[2], ball_Y[3]);
  and and_3 (and_3_out, ball_Y[0], ball_Y[1], ball_Y[2], ball_Y[3]);
  and and_4 (and_4_out[3], ~nor_2_out, ~Y_direction__1_plus);  // AND_Gate
  and and_5 (and_5_out, and_1_out, and_3_out);
  and and_6 (and_6_out, Y_direction__1_plus, ~and_3_out);  // AND_Gate
  // Probe on adder_2_out
  Adder #(.width(4)) adder_2 (.a(ball_Y), .b({4{and_4_out[3]}}), .out(adder_2_out), .cin(and_6_out));  // open: cout
  Comparator #(.width(4), .mode("unsigned")) comparator_1 (
    .a(adder_1_out), .b(adder_2_out), .gt(comparator_1_gt), .eq(comparator_1_eq));  // open: lt
  Comparator #(.width(4), .mode("unsigned")) comparator_2 (
    .a(board_pos), .b(adder_2_out), .eq(comparator_2_eq), .lt(comparator_2_lt));  // open: gt
  or or_1 (or_1_out, comparator_2_lt, comparator_2_eq);
  or or_2 (or_2_out, comparator_1_eq, comparator_1_gt);
  and and_7 (and_7_out, or_2_out, or_1_out);
  or or_3 (or_3_out, and_7_out, and_5_out, and_2_out);
  and and_8 (match, ~or_3_out, ball_X_1);  // AND_Gate
endmodule
